# Fritzing sketch Kluisje (saved by Fritzing 0.9.3b)

parts:
  Onderdeel1 = Arduino Uno (Rev3) - ICSP
  PIR1 = PIR sensor
  Q1 = npn-Powertransistor [package="TO220 [THT]"]
  Q2 = npn-Powertransistor [package="TO220 [THT]"]
  Q3 = npn-Powertransistor [package="TO220 [THT]"]
  Q4 = npn-Powertransistor [package="TO220 [THT]"]
  VALVE1 = Plastic Solenoid Valve
  VCC1 = Battery block 9V

nets:
  N1: Onderdeel1.D8, Q1.base
  N2: Onderdeel1.D9_PWM, Q2.base
  N3: Onderdeel1.D10_PWM/SS, Q3.base
  N4: Onderdeel1.D11_PWM/MOSI, Q4.base
  N5: Onderdeel1.D4, PIR1.SIG
  GND: Onderdeel1.GND, PIR1.GND, Q1.emitter, Q2.emitter, Q3.emitter, Q4.emitter, VCC1.-
  N6: Q1.collector, Q2.collector, Q4.collector, VALVE1.no_name_yet#1
  N7: VALVE1.no_name_yet#2, VCC1.+

notes:
  Fingerprint Sensor
  12 Volt 1A
  Solenoid Lock
